// Digital circuit Punto_1_Multiplexor_8_Entradas.dig as structural Verilog
module Punto_1_Multiplexor_8_Entradas (
  input  Sel_0,
  input  Sel_1,
  input  Sel_2,
  input  D_0,
  input  D_1,
  input  D_2,
  input  D_3,
  input  D_4,
  input  D_5,
  input  D_6,
  input  D_7,
  output OUTPUT
);

  wire and_1_out, and_2_out, and_3_out, and_4_out, and_5_out, and_6_out, and_7_out, and_8_out, not_1_out,
       not_2_out, not_3_out, or_1_out, or_2_out;

  not not_1 (not_1_out, Sel_0);
  not not_2 (not_2_out, Sel_1);
  not not_3 (not_3_out, Sel_2);
  and and_1 (and_1_out, not_1_out, not_2_out, not_3_out, D_0);
  and and_2 (and_2_out, Sel_0, not_2_out, not_3_out, D_1);
  and and_3 (and_3_out, not_1_out, Sel_1, not_3_out, D_2);
  and and_4 (and_4_out, Sel_0, Sel_1, not_3_out, D_3);
  and and_5 (and_5_out, not_1_out, not_2_out, Sel_2, D_4);
  and and_6 (and_6_out, Sel_0, not_2_out, Sel_2, D_5);
  and and_7 (and_7_out, not_1_out, Sel_1, Sel_2, D_6);
  and and_8 (and_8_out, Sel_0, Sel_1, Sel_2, D_7);
  or or_1 (or_1_out, and_1_out, and_2_out, and_3_out, and_4_out);
  or or_2 (or_2_out, and_5_out, and_6_out, and_7_out, and_8_out);
  or or_3 (OUTPUT, or_1_out, or_2_out);

  // Notes on the sheet:
  //   Respetado usuario: 
  //   El siguiente circuito presenta un multiplexor con relación 8:1 (8 entradas con una única salida).
  //   Sean las entradas D_0,D_1,D_2...,D_7 los estados posibles (altos o bajos) que usted ingresará.
  //   Además considere los botones Sel-0,Sel-1 y Sel-2 como las combinaciones de entradas de control.
  //   Este circuito originalmente combinacional presenta una secuencia lógica con compuertas
  //   AND y OR de 2 y 4 entradas, que básicamente compara la entrada que usted ingresa con una 
  //   segunda combinación de botones de control (Sel-0, Sel_1 y Sel_2) que en últimas representan 
  //   el exponente al que se eleva el 2 en cada casilla de la conversión sexagesimal-binaria.
  //   MULTIPLEXOR PARA 8 ENTRADAS.
  //   Ejemplo: Si se consideran 3 Bits, se conoce que se pueden representar 8 posibles valores 
  //   de voltaje (incluyendo el 0) considerando que para cada una de las casillas de conversión
  //   solo existirá un valor de 0 ó 1 (bajo o alto). 
  //   Por ello, la salida OUTPUT solo tendrá un valor de 1 sí y solo sí el valor ingresado en D_n 
  //   corresponde con el exponente del 2 correspondiente a ese valor en los botones de 
  //   control (Sel-0,Sel-1,Sel-2). 
  //   A modo de experiencia, si se ingresa alto solo en la entrada D_3, para obtenerse alto en OUTPUT 
  //   deben ingresarse en alto los controles Sel-0 y Sel-1 dado que el número tres es 2 elevado a la 0 
  //   más 2 elevado a la 1.
endmodule
