// Digital circuit Punto_2_Demux_4_Salidas.dig as structural Verilog
module Punto_2_Demux_4_Salidas (
  input  Sel_1,
  input  Sel_0,
  input  IN,
  output Out_3,
  output Out_2,
  output Out_1,
  output Out_0
);

  wire not_1_out, not_2_out;

  not not_1 (not_1_out, Sel_1);
  not not_2 (not_2_out, Sel_0);
  and and_1 (Out_3, IN, Sel_1, Sel_0);
  and and_2 (Out_2, IN, Sel_1, not_2_out);
  and and_3 (Out_1, IN, not_1_out, Sel_0);
  and and_4 (Out_0, IN, not_1_out, not_2_out);

  // Notes on the sheet:
  //   Tomando como referencia el punto anterior, para este caso 
  //   se tienen únicamente 4 posibles valores de representación 
  //   a la salida del demultiplexor, que hace la conversión contraria 
  //   al anterior. 
  //   La entrada IN representa encender o apagar el circuito. 
  //   Ejemplo: 
  //   Si se desea obtener por ejemplo Out_1 a la salida, 
  //   debe encenderse el botón de control Sel_0 y el "enable" IN,
  //   dado que 2 a la 0 es 1.
  //   DEMULTIPLEXOR (DEMUX) PARA 4 SALIDAS.
endmodule
