// Digital circuit Punto_3A_FlipFlop_RS.dig as structural Verilog
module Punto_3A_FlipFlop_RS (
  input  In_S,
  input  In_R,
  input  Clock,
  output Out_Q,
  output Out_Q_2
);

  wire nand_1_out, nand_2_out, nand_3_out, nand_4_out, nand_5_out, nand_6_out, not_1_out;

  not not_1 (not_1_out, Clock);
  nand nand_1 (nand_1_out, In_S, not_1_out);
  nand nand_2 (nand_2_out, not_1_out, In_R);
  nand nand_3 (nand_3_out, nand_1_out, nand_4_out);
  nand nand_4 (nand_4_out, nand_3_out, nand_2_out);
  nand nand_5 (nand_5_out, nand_3_out, Clock);
  nand nand_6 (nand_6_out, Clock, nand_4_out);
  nand nand_7 (Out_Q, nand_5_out, Out_Q_2);
  nand nand_8 (Out_Q_2, Out_Q, nand_6_out);

  // Notes on the sheet:
  //   Se definen las entradas "In S" e "In R", que provienen del inglés Set "poner" y Reset "quitar". 
  //   Además, una tercera entrada Clock que hace las veces de reloj, mediante la cual usted, 
  //   señor usuario, podrá controlar el almacenamiento de datos.
  //   Este sistema le permite observar el principio básico de funcionamiento de una memoria, 
  //   que mediante la articulación de dos latch (Un latch es básicamente un circuito cerrojo, conociendo 
  //   el primero como máster y el segundo de izquierda a derecha como slave) permite almacenar 
  //   un dato con dos posibles estados (alto y bajo, por esto se llama biestable) redirigiendolo 
  //   mediante compuertas lógicas NAND y NOT de 2 entradas a una salida que lo almacena o a otra 
  //   que lo borra, a una frecuencia de muestreo que usted mismo determina accionando el reloj "Clock". 
  //   Note, además que el sistema se actualiza en el llamado flanco de subida, que ocurre cuando el botón 
  //   del reloj va desde 0 hasta 1 y se mantiene estable de 1 a 0, es decir, no cambia.
  //   Nota: Si ambas entradas In S e In R se encuentran encendidas y se actualiza el circuito (Uso del Clock),
  //   la lógica del sistema entra en conflicto.
  //   FLIP-FLOP TIPO RS
endmodule
