// Digital circuit Punto_3B_FlipFlop_JK.dig as structural Verilog
module Punto_3B_FlipFlop_JK (
  input  In_K,
  input  In_J,
  input  Clock,
  output Out_Q,
  output Out_Q_2
);

  wire and_1_out, and_2_out, nand_1_out, nand_2_out, nand_3_out, nand_4_out, nor_1_out, nor_2_out, not_1_out,
       not_2_out, not_3_out;

  nand nand_1 (nand_1_out, Out_Q, In_K);
  not not_1 (not_1_out, Clock);
  nand nand_2 (nand_2_out, In_J, Out_Q_2);
  not not_2 (not_2_out, nand_1_out);
  not not_3 (not_3_out, nand_2_out);
  and and_1 (and_1_out, not_2_out, not_1_out);
  and and_2 (and_2_out, not_1_out, not_3_out);
  nor nor_1 (nor_1_out, and_1_out, nor_2_out);
  nor nor_2 (nor_2_out, nor_1_out, and_2_out);
  nand nand_3 (nand_3_out, nor_1_out, Clock);
  nand nand_4 (nand_4_out, Clock, nor_2_out);
  nand nand_5 (Out_Q, nand_3_out, Out_Q_2);
  nand nand_6 (Out_Q_2, Out_Q, nand_4_out);

  // Notes on the sheet:
  //   Considere las entradas In K e In J que usted ingresará a voluntad. 
  //   Además, la señal de entrada Clock representa el reloj del sistema cuya 
  //   frecuencia determinará usted de acuerdo a su necesidad. Note 
  //   que esta señal actualiza el sistema cuando está en alto y la mantiene estable
  //   cuando está en bajo.
  //   La disposición de este circuito es bastante similar al Flip Flop RS
  //   presentado en el punto anterior. Funciona de una manera similar 
  //   pero soluciona el error que se presentaba al encender las dos entradas
  //   del circuito que para este caso son J y K. Cuando se encienden en modo 
  //   alto estas dos entradas y se actualiza con la señal del reloj (Clock) la lógica 
  //   del sistema comienza a oscilar, encendiendo las salidas Out Q y Out Q´de 
  //   manera alternada conforme se va actualizando el clock. Claramente, este circuito 
  //   es una forma elegante y muy usual de almacenamiento y de datos.
  //   FLIP-FLOP TIPO JK.
endmodule
