// Digital circuit Punto_4_Registro_4_Bits.dig as structural Verilog
module Punto_4_Registro_4_Bits (
  input  D_1,
  input  Enable_1,
  input  Set_1,
  input  Clear,
  input  In_1,
  input  D_2,
  input  In_2,
  input  D_3,
  input  In_3,
  input  D_4,
  input  In_4,
  input  Enable_2,
  input  E_1,
  input  Set_2,
  input  Clear_2,
  input  E_2,
  input  E_3,
  input  E_4,
  input  Enable_3,
  input  Set_3,
  input  Clear_3,
  input  Clock,
  output Out_micro_1,
  output Out_micro2,
  output Out_micro3,
  output Out_micro4,
  output out_25,
  output out_27,
  output out_28,
  output out_29
);

  wire d_ff_as_1_q, d_ff_as_2_q, d_ff_as_3_q, d_ff_as_4_q, In_1_t, In_2_t, In_3_t, In_4_t, multiplexer_1_out,
       multiplexer_2_out, multiplexer_3_out, multiplexer_4_out, multiplexer_5_out, multiplexer_6_out,
       multiplexer_7_out, multiplexer_8_out, multiplexer_9_out, multiplexer_10_out, multiplexer_11_out,
       multiplexer_12_out, Out_1, Out_2, Out_3, Out_4;

  Multiplexer multiplexer_1 (.sel(Enable_1), .in_0(d_ff_as_1_q), .in_1(D_1), .out(multiplexer_1_out));
  D_FF_AS d_ff_as_1 (.Set(Set_1), .D(multiplexer_1_out), .C(Clock), .Clr(Clear), .Q(d_ff_as_1_q));  // open: nQ
  assign Out_micro_1 = ~d_ff_as_1_q ? Out_1 : 1'bz;  // DriverInvSel driverinvsel_1
  assign In_1_t = d_ff_as_1_q ? In_1 : 1'bz;  // Driver driver_1
  Multiplexer multiplexer_2 (.sel(Enable_1), .in_0(d_ff_as_2_q), .in_1(D_2), .out(multiplexer_2_out));
  D_FF_AS d_ff_as_2 (.Set(Set_1), .D(multiplexer_2_out), .C(Clock), .Clr(Clear), .Q(d_ff_as_2_q));  // open: nQ
  assign Out_micro2 = ~d_ff_as_2_q ? Out_2 : 1'bz;  // DriverInvSel driverinvsel_2
  assign In_2_t = d_ff_as_2_q ? In_2 : 1'bz;  // Driver driver_2
  Multiplexer multiplexer_3 (.sel(Enable_1), .in_0(d_ff_as_3_q), .in_1(D_3), .out(multiplexer_3_out));
  D_FF_AS d_ff_as_3 (.Set(Set_1), .D(multiplexer_3_out), .C(Clock), .Clr(Clear), .Q(d_ff_as_3_q));  // open: nQ
  assign Out_micro3 = ~d_ff_as_3_q ? Out_3 : 1'bz;  // DriverInvSel driverinvsel_3
  assign In_3_t = d_ff_as_3_q ? In_3 : 1'bz;  // Driver driver_3
  Multiplexer multiplexer_4 (.sel(Enable_1), .in_0(d_ff_as_4_q), .in_1(D_4), .out(multiplexer_4_out));
  D_FF_AS d_ff_as_4 (.Set(Set_1), .D(multiplexer_4_out), .C(Clock), .Clr(Clear), .Q(d_ff_as_4_q));  // open: nQ
  assign Out_micro4 = ~d_ff_as_4_q ? Out_4 : 1'bz;  // DriverInvSel driverinvsel_4
  assign In_4_t = d_ff_as_4_q ? In_4 : 1'bz;  // Driver driver_4
  Multiplexer multiplexer_5 (.sel(Enable_2), .in_0(Out_1), .in_1(E_1), .out(multiplexer_5_out));
  PullDown pulldown_1 (.out(In_1_t));
  Multiplexer multiplexer_6 (.sel(Enable_3), .in_0(out_25), .in_1(In_1_t), .out(multiplexer_6_out));
  D_FF_AS d_ff_as_5 (.Set(Set_2), .D(multiplexer_5_out), .C(Clock), .Clr(Clear_2), .Q(Out_1));  // open: nQ
  D_FF_AS d_ff_as_6 (.Set(Set_3), .D(multiplexer_6_out), .C(Clock), .Clr(Clear_3), .Q(out_25));  // open: nQ
  Multiplexer multiplexer_7 (.sel(Enable_3), .in_0(out_27), .in_1(In_2_t), .out(multiplexer_7_out));
  Multiplexer multiplexer_8 (.sel(Enable_2), .in_0(Out_2), .in_1(E_2), .out(multiplexer_8_out));
  PullDown pulldown_2 (.out(In_2_t));
  D_FF_AS d_ff_as_7 (.Set(Set_3), .D(multiplexer_7_out), .C(Clock), .Clr(Clear_3), .Q(out_27));  // open: nQ
  D_FF_AS d_ff_as_8 (.Set(Set_2), .D(multiplexer_8_out), .C(Clock), .Clr(Clear_2), .Q(Out_2));  // open: nQ
  PullDown pulldown_3 (.out(In_3_t));
  Multiplexer multiplexer_9 (.sel(Enable_3), .in_0(out_28), .in_1(In_3_t), .out(multiplexer_9_out));
  D_FF_AS d_ff_as_9 (.Set(Set_3), .D(multiplexer_9_out), .C(Clock), .Clr(Clear_3), .Q(out_28));  // open: nQ
  Multiplexer multiplexer_10 (.sel(Enable_2), .in_0(Out_3), .in_1(E_3), .out(multiplexer_10_out));
  D_FF_AS d_ff_as_10 (.Set(Set_2), .D(multiplexer_10_out), .C(Clock), .Clr(Clear_2), .Q(Out_3));  // open: nQ
  Multiplexer multiplexer_11 (.sel(Enable_3), .in_0(out_29), .in_1(In_4_t), .out(multiplexer_11_out));
  PullDown pulldown_4 (.out(In_4_t));
  D_FF_AS d_ff_as_11 (.Set(Set_3), .D(multiplexer_11_out), .C(Clock), .Clr(Clear_3), .Q(out_29));  // open: nQ
  Multiplexer multiplexer_12 (.sel(Enable_2), .in_0(Out_4), .in_1(E_4), .out(multiplexer_12_out));
  D_FF_AS d_ff_as_12 (.Set(Set_2), .D(multiplexer_12_out), .C(Clock), .Clr(Clear_2), .Q(Out_4));  // open: nQ

  // Other names for the same wires on the sheet: Clock_Out = Clock

  // Notes on the sheet:
  //   Clock: Hz: 10
  //   (1) CONFIGURACIÓN ENTRADA SALIDA:
  //   Considere para este y los circuitos posteriores (2) y (3) Las entradas Enable_n (Botón de control para permitir el flujo de datos)
  //   y los botones Set_n (Para configurar todos los bloques como entrada o salida inmediatamente), junto con un reloj Clock que es 
  //   común para todos. 
  //   La configuración entrada o salida se asume para D_n = 1 como entrada y D_n = 0 como salida. 
  //   Si la configuración inicial resulta ser una entrada (Flujo externo hacia el microcontrolador) se habilitan las entradas In_n
  //   que son los datos que ingresarán al microcontrolador. De allí, teniendo esta configuración como entrada, luego de ingresar
  //   este dato In_n el flujo se sigue hacia el circuito (3).
  //   Los siguientes circuitos representan el flujo de configuración básico para un pin I/O de un microcontrolador. 
  //   Por tanto, se enumeran los circuitos de acuerdo con su función del (1) al (3).
  //   NOTA: La entrada Clear en cada circuito sirve para regresar al estado inicial el circuito, limpiando los datos.
  //   CONFIGURACIONES PARA PIN I/O.
  //   (2) Circuito salida. 
  //   Si la configuración en (1) fue como salida, el microcontrolador envía un dato E_n desde su procesamiento interno hacia su exterior (a un pin). 
  //   Por tanto, si se configura en modo salida y se envía un dato E_n = 1 desde dentro del microcontrolador, el impulso se transmitirá hacia las 
  //   correspondientes salidas Out_micro-n que se visualizan en la parte externa del microcontrolador en el circuito de la configuración entrada/salida (1).
  //   (3) Circuito entrada. 
  //   Si la configuración en (1) fue como entrada, el microcontrolador almacena la entrada In_n dada en 1 siguiendo la lógica
  //   del siguiente registro, que básicamente consta de un multiplexor y un flip flop que conducen ese dato In_n a cada una de 
  //   las salidas que son el impulso interno que genera el microcontrolador (guardando el dato).
endmodule
